# Fritzing sketch only-usage (saved by Fritzing 0.9.3b)
circuit board: 8.46667cm x 5.64444cm
perfboards: 1

parts:
  J1 = female pin header, 4 pins [form="♀ (female)"]
  ESP-01_Connector = female pin header, 4 pins [form="♀ (female)"]
  VCC_-_GND = Battery block 9V
  C2 = Electrolytic Capacitor [capacitance=10µF package="100 mil [THT, electrolytic]"]
  R1 = Resistor [tolerance=±5% resistance=5.6k package="2512 [SMD]"]
  R2 = Resistor [tolerance=±5% resistance=3.3k package="2512 [SMD]"]
  U1 = Voltage Regulator [package=to220-adj]

nets:
  N1: J1.pin2, ESP-01_Connector.pin1, ESP-01_Connector.pin3, C2.+, R2.Pin_0, U1.OUT
  N2: J1.pin4, VCC_-_GND.-, C2.-, R1.Pin_0
  N3: VCC_-_GND.+, U1.IN
  N4: R1.Pin_1, R2.Pin_1, U1.ADJ
